// Logisim project Laboratorio3.circ as structural Verilog: 11 circuits, main circuit ALU
module ALU (
  input  [31:0] X,
  input  [31:0] Y,
  input  [3:0] SelectALU,
  output [31:0] result,
  output ZeroResult
);

  wire comparator_1_eq, comparator_1_lt;
  wire [31:0] adder_1_out, and_1_out, bit_extender_1_out, bit_extender_2_out, divider_1_out, nor_1_out,
       or_1_out, or_2_out, shifter_1_out, subtractor_1_out;

  assign and_1_out = X & Y;  // AND_Gate and_1, 32 bits wide
  assign or_1_out = X | Y;  // OR_Gate or_1, 32 bits wide
  assign nor_1_out = ~(X | Y);  // NOR_Gate nor_1, 32 bits wide
  Adder #(.width(32)) adder_1 (.a(X), .b(Y), .out(adder_1_out));  // open: cin, cout
  Subtractor #(.width(32)) subtractor_1 (.a(X), .b(Y), .out(subtractor_1_out));  // open: bin, bout
  Shifter #(.width(32)) shifter_1 (.in(Y), .\dist (X[4:0]), .out(shifter_1_out));
  Divider #(.width(32)) divider_1 (.a(X), .b(Y), .out(divider_1_out));  // open: upper, rem
  Comparator #(.mode("unsigned"), .width(32)) comparator_1 (
    .a(X), .b(Y), .eq(comparator_1_eq), .lt(comparator_1_lt));  // open: gt
  assign bit_extender_1_out = {{31{comparator_1_eq}}, comparator_1_eq};  // Bit_Extender bit_extender_1
  assign bit_extender_2_out = {{31{comparator_1_lt}}, comparator_1_lt};  // Bit_Extender bit_extender_2
  assign or_2_out = bit_extender_1_out | bit_extender_2_out;  // OR_Gate or_2, 32 bits wide
  Multiplexer #(.select(4), .width(32)) multiplexer_1 (
    .in0(and_1_out), .in1(or_1_out), .in2(adder_1_out), .in6(subtractor_1_out), .in7(or_2_out),
    .in11(divider_1_out), .in12(nor_1_out), .in14(shifter_1_out), .out(result), .sel(SelectALU));  // open: in3, in4, in5, in8, in9, in10, in13, in15
  Comparator #(.width(32)) comparator_2 (.a(result), .b({32{1'b0}}), .eq(ZeroResult));  // open: gt, lt

  // Notes on the sheet:
  //   1101 DIV
  //   0000  AND
  //   0001  OR
  //   0010 ADD
  //   0110 SUBSTRACT
  //   0111 SET ON LESS THAN
  //   1100 NOR
  //   1010 MULT
endmodule

module ProgramCounter (
  input  [31:0] Instruction,
  input  Clk,
  input  Reset,
  output [31:0] Address
);

  Register #(.width(32)) register_1 (.D(Instruction), .en(1'b1), .clk(Clk), .Q(Address), .clr(Reset));
endmodule

module main (
  input  Reset,
  output [31:0] out_2
);

  wire alu_3_zeroresult, and_1_out, and_2_out, Clk_out, comparator_1_eq, controllerunit_1_alusrc,
       controllerunit_1_branch, controllerunit_1_jump, controllerunit_1_jump_jal, controllerunit_1_jump_jr,
       controllerunit_1_memread, controllerunit_1_memtoreg, controllerunit_1_memwrite,
       controllerunit_1_regdst, controllerunit_1_regwrite, controllerunit_1_zero, not_1_out;
  wire [1:0] controllerunit_1_aluop;
  wire [3:0] alu_1_result, controlalu_1_aluoperation;
  wire [4:0] mux_1_salida;
  wire [27:0] alu_1_result_2;
  wire [31:0] alu_2_result, alu_3_result, bit_extender_1_out, datamemory_1_readdata, multiplexer_1_out,
       mux_32_1_salida, mux_32_2_salida, mux_32_3_salida, mux_32_4_salida, mux_32_5_salida, mux_32_6_salida,
       programcounter_1_address, registers_1_p8, registers_1_p9, shiftleft2_1_salida, sign_extend_1_extend;

  Clock Clk (.out(Clk_out));
  ProgramCounter programcounter_1 (
    .Instruction(mux_32_5_salida), .Clk(Clk_out), .Reset(Reset), .Address(programcounter_1_address));
  MemoryInstruction memoryinstruction_1 (.Address(programcounter_1_address), .Instruction(out_2));
  MUX_32 mux_32_1 (
    .Instruction1(mux_32_6_salida), .Instruction2({alu_1_result, alu_1_result_2}),
    .Selector(controllerunit_1_jump_jal), .Salida(mux_32_1_salida));
  ControllerUnit controllerunit_1 (
    .opcode(out_2[31:26]), .RegDst(controllerunit_1_regdst), .ALUSrc(controllerunit_1_alusrc),
    .MemtoReg(controllerunit_1_memtoreg), .RegWrite(controllerunit_1_regwrite),
    .MemRead(controllerunit_1_memread), .MemWrite(controllerunit_1_memwrite),
    .Branch(controllerunit_1_branch), .ALUOp(controllerunit_1_aluop), .jump(controllerunit_1_jump),
    .jump_jr(controllerunit_1_jump_jr), .jump_jal(controllerunit_1_jump_jal), .Zero(controllerunit_1_zero));
  ALU alu_1 (
    .X(programcounter_1_address), .Y(32'h1), .SelectALU(4'b0010), .result({alu_1_result, alu_1_result_2}));  // open: ZeroResult
  MUX mux_1 (
    .Instruction1(out_2[20:16]), .Instruction2(out_2[15:11]), .Selector(controllerunit_1_regdst),
    .Salida(mux_1_salida));
  // Registers registers_1: pin names not known; wires that end beside it: out_2[25:21], out_2[20:16], mux_1_salida, mux_32_1_salida, Clk_out, controllerunit_1_regwrite, Reset, registers_1_p8, registers_1_p9
  Sign_extend sign_extend_1 (.Entrada(out_2[15:0]), .Extend(sign_extend_1_extend));
  ShiftLeft2 shiftleft2_1 (.Entrada(sign_extend_1_extend), .Salida(shiftleft2_1_salida));
  MUX_32 mux_32_2 (
    .Instruction1(registers_1_p9), .Instruction2(sign_extend_1_extend), .Selector(controllerunit_1_alusrc),
    .Salida(mux_32_2_salida));
  Comparator #(.mode("unsigned"), .width(5)) comparator_1 (
    .a(out_2[10:6]), .b({5{1'b0}}), .eq(comparator_1_eq));  // open: gt, lt
  assign bit_extender_1_out = {{27{1'b0}}, out_2[10:6]};  // Bit_Extender bit_extender_1
  not not_1 (not_1_out, comparator_1_eq);
  ALU alu_2 (
    .X({alu_1_result, alu_1_result_2}), .Y(shiftleft2_1_salida), .SelectALU(4'b0010), .result(alu_2_result));  // open: ZeroResult
  ALU alu_3 (
    .X(multiplexer_1_out), .Y(mux_32_2_salida), .SelectALU(controlalu_1_aluoperation), .result(alu_3_result),
    .ZeroResult(alu_3_zeroresult));
  Multiplexer #(.width(32)) multiplexer_1 (
    .in0(registers_1_p8), .in1(bit_extender_1_out), .out(multiplexer_1_out), .sel(and_1_out));
  ControlALU controlalu_1 (
    .ALUOp(controllerunit_1_aluop), .funct(out_2[5:0]), .ALUOperation(controlalu_1_aluoperation));
  and and_1 (and_1_out, not_1_out, controllerunit_1_zero);
  MUX_32 mux_32_3 (
    .Instruction1({alu_1_result, alu_1_result_2}), .Instruction2(alu_2_result), .Selector(and_2_out),
    .Salida(mux_32_3_salida));
  and and_2 (and_2_out, controllerunit_1_branch, alu_3_zeroresult);
  MUX_32 mux_32_4 (
    .Instruction1(mux_32_3_salida), .Instruction2({alu_1_result, 2'b00, out_2[25:0]}),
    .Selector(controllerunit_1_jump), .Salida(mux_32_4_salida));
  DataMemory datamemory_1 (
    .Address(alu_3_result), .WriteData(registers_1_p9), .Clk(Clk_out), .MemoryRead(controllerunit_1_memread),
    .MemoryWrite(controllerunit_1_memwrite), .ReadData(datamemory_1_readdata));
  MUX_32 mux_32_5 (
    .Instruction1(mux_32_4_salida), .Instruction2(registers_1_p8), .Selector(controllerunit_1_jump_jr),
    .Salida(mux_32_5_salida));
  MUX_32 mux_32_6 (
    .Instruction1(alu_3_result), .Instruction2(datamemory_1_readdata), .Selector(controllerunit_1_memtoreg),
    .Salida(mux_32_6_salida));
endmodule

module MemoryInstruction (
  input  [31:0] Address,
  output [31:0] Instruction
);

  ROM #(.dataWidth(32)) rom_1 (.addr(Address[7:0]), .data(Instruction));

  // Notes on the sheet:
  //   contents of rom_1 (hex, n*v repeats v):
  //   3c110000 c1f0008 3c040000 22050000 c1f000e 20450000 c1f0013 8000017 8e240000 10800003 22100001
  //   22310001 8000008 7e00008 214a0002 aa4822 2499020 8e420000 7e00008 55980 56100 16c1820 7e00008
  //   22b50014 aea30000
endmodule

module MUX (
  input  [4:0] Instruction1,
  input  [4:0] Instruction2,
  input  Selector,
  output [4:0] Salida
);

  Multiplexer #(.width(5)) multiplexer_1 (.in0(Instruction1), .in1(Instruction2), .out(Salida), .sel(Selector));
endmodule

module MUX_32 (
  input  [31:0] Instruction1,
  input  [31:0] Instruction2,
  input  Selector,
  output [31:0] Salida
);

  Multiplexer #(.width(32)) multiplexer_1 (.in0(Instruction1), .in1(Instruction2), .out(Salida), .sel(Selector));
endmodule

module Sign_extend (
  input  [15:0] Entrada,
  output [31:0] Extend
);

  assign Extend = {{16{Entrada[15]}}, Entrada};  // Bit_Extender bit_extender_1
endmodule

module DataMemory (
  input  [31:0] Address,
  input  MemoryWrite,
  input  MemoryRead,
  input  Clk,
  input  [31:0] WriteData,
  output [31:0] ReadData
);

  RAM #(.asyncread("true"), .dataWidth(32)) ram_1 (
    .addr(Address[7:0]), .we(MemoryWrite), .oe(MemoryRead), .clk(Clk), .din(WriteData), .dout(ReadData));
endmodule

module ShiftLeft2 (
  input  [31:0] Entrada,
  output [31:0] Salida
);

  Shifter #(.width(32)) shifter_1 (.in(Entrada), .\dist (5'b00010), .out(Salida));
endmodule

module ControlALU (
  input  [1:0] ALUOp,
  input  [5:0] funct,
  output [3:0] ALUOperation
);

  wire and_1_out, and_2_out, and_3_out, and_4_out, and_5_out, not_1_out, not_2_out, not_3_out, not_4_out,
       not_5_out;

  not not_1 (not_1_out, ALUOp[1]);
  not not_2 (not_2_out, ALUOp[0]);
  not not_3 (not_3_out, funct[5]);
  not not_4 (not_4_out, funct[2]);
  not not_5 (not_5_out, funct[1]);
  and and_1 (and_1_out, ALUOp[1], not_2_out, not_3_out);
  and and_2 (and_2_out, ALUOp[1], not_2_out, funct[2], funct[1]);
  and and_3 (and_3_out, ALUOp[1], not_2_out, not_3_out);
  and and_4 (and_4_out, ALUOp[1], not_2_out, funct[1]);
  and and_5 (and_5_out, not_1_out, ALUOp[0]);
  or or_1 (ALUOperation[1], not_1_out, not_4_out, ALUOp[0]);
  and and_6 (ALUOperation[0], ALUOp[1], not_2_out, not_5_out, funct[0]);
  or or_2 (ALUOperation[3], and_1_out, and_2_out);
  or or_3 (ALUOperation[2], and_3_out, and_4_out, and_5_out);
endmodule

module ControllerUnit (
  input  [5:0] opcode,
  output RegDst,
  output ALUSrc,
  output MemtoReg,
  output RegWrite,
  output MemRead,
  output MemWrite,
  output Branch,
  output [1:0] ALUOp,
  output jump,
  output jump_jr,
  output jump_jal,
  output Zero
);

  wire and_2_out, and_3_out, and_5_out, and_6_out, and_7_out, and_11_out, and_12_out, and_13_out, and_14_out,
       not_1_out, not_2_out, not_3_out, not_4_out, not_5_out, not_6_out;

  not not_1 (not_1_out, opcode[5]);
  not not_2 (not_2_out, opcode[4]);
  not not_3 (not_3_out, opcode[3]);
  not not_4 (not_4_out, opcode[2]);
  not not_5 (not_5_out, opcode[1]);
  not not_6 (not_6_out, opcode[0]);
  and and_1 (RegDst, not_6_out, not_5_out, not_3_out, not_2_out, not_1_out);
  and and_2 (and_2_out, opcode[5], not_2_out, not_4_out, opcode[1], opcode[0]);
  and and_3 (and_3_out, not_1_out, not_2_out, opcode[3]);
  and and_4 (MemtoReg, opcode[0], opcode[1], not_4_out, not_2_out, opcode[5]);
  and and_5 (and_5_out, not_1_out, not_2_out, not_4_out, not_5_out, not_6_out);
  and and_6 (and_6_out, not_2_out, not_3_out, not_4_out, opcode[1], opcode[0]);
  and and_7 (and_7_out, not_1_out, not_2_out, opcode[3]);
  and and_8 (MemRead, opcode[0], opcode[1], not_4_out, not_3_out, not_2_out, opcode[5]);
  and and_9 (MemWrite, opcode[0], opcode[1], not_4_out, opcode[3], not_2_out, opcode[5]);
  and and_10 (Branch, not_6_out, not_5_out, opcode[2], not_3_out, not_2_out, not_1_out);
  and and_11 (and_11_out, not_1_out, not_2_out, not_4_out, not_5_out, not_6_out);
  and and_12 (and_12_out, not_1_out, not_2_out, opcode[3]);
  and and_13 (and_13_out, not_1_out, not_2_out, opcode[2], not_5_out, not_6_out);
  and and_14 (and_14_out, not_1_out, not_2_out, opcode[3]);
  and and_15 (jump, not_1_out, not_2_out, not_3_out, not_4_out, opcode[1]);
  and and_16 (jump_jr, not_1_out, not_2_out, not_3_out, not_4_out, not_5_out, opcode[0]);
  and and_17 (jump_jal, not_1_out, not_2_out, not_3_out, not_4_out, opcode[1], opcode[0]);
  or or_1 (ALUSrc, and_2_out, and_3_out);
  or or_2 (RegWrite, and_5_out, and_6_out, and_7_out);
  or or_3 (ALUOp[1], and_11_out, and_12_out);
  or or_4 (ALUOp[0], and_13_out, and_14_out);
  Comparator #(.mode("unsigned"), .width(6)) comparator_1 (.a(opcode), .b({6{1'b0}}), .eq(Zero));  // open: gt, lt
endmodule
